# Fritzing sketch schema (saved by Fritzing 0.9.2b)

parts:
  U1 = 4RelayModule
  Součástka1 = Arduino Uno (Rev3) - ICSP  # not connected
  Součástka2 = Arduino Board Ethernet
  Součástka3 = Tiny RTC - DS1307 Breakout Board
  U2 = TMP36 [package=to-92-kit]
  R1 = Resistor [tolerance=±5% resistance=4.7k package="0603 [SMD]"]
  S1 = Momentary Switch [package=ksa_sealed_tac_switch]
  R2 = Resistor [tolerance=±5% resistance=15k package="0603 [SMD]"]

nets:
  N1: U1.IN2, Součástka2.D4
  N2: U1.IN1, Součástka2.D3_PWM
  N3: U1.IN3, Součástka2.D5_PWM
  GND: Součástka2.GND, U2.GND
  N4: Součástka2.A0, S1.1
  N5: Součástka2.A4, Součástka3.SDA
  N6: Součástka2.A5, Součástka3.SCL
  N7: Součástka2.D2_PWM, U2.VOUT, R1.Pin_0
  N8: Součástka2.3V3, R2.Pin_0
  N9: S1.3, R2.Pin_1

notes:
  DS18B20
  ULN2003
  Water level switch
  Feeder for fish
  relay on lights, filter, heater
  time
  water temperature

custom parts:
  4RelayModule: 4 relay arduino module SONGLE SRD05VDC-SL-C
  Tiny RTC - DS1307 Breakout Board: The Tiny RTC is a breakout board for the Dallas Semiconductor/Maxim Integrated DS1307 real-time clock. The DS1307 counts seconds, minutes, hours, date of the month, month, day of the week, and year (with compensation for leap-years). The breakout board also has space for a DS18B20 digital thermometer.
